# Fritzing sketch Interval-O-Meter (saved by Fritzing 0.9.2b)
circuit board: 8.46667cm x 5.64444cm
breadboards: 1

parts:
  U1 = 2.5mm Audio Jack [package=stereojack2.5mm_specia_pogopins]
  JACK1 = 2.1mm Barrel Jack with Terminal Block
  Q1 = NPN-Transistor [package="TO92 [THT]"]
  Q2 = NPN-Transistor [package="TO92 [THT]"]
  U2 = attiny85 [package=dip]
  R1 = Resistor [tolerance=±5% resistance=10k package=THT]
  R2 = Resistor [tolerance=±5% resistance=10k package=THT]
  U4 = SWITCH-SPST-2 [package=r_sw_th]
  U5 = SWITCH-SPST-2 [package=r_sw_th]
  R5 = Rotary Potentiometer (Large) [maximum_resistance=100kΩ package=THT]
  R3 = Resistor [tolerance=±5% resistance=220 package=THT]
  R4 = Resistor [tolerance=±5% resistance=220 package=THT]
  U6 = SWITCH-SPST-2 [package=r_sw_th]
  LED1 = RGB LED (com. cathode, rgb) [package="5 mm [THT]"]

nets:
  N1: U1.SLEEVE, JACK1.NEG, Q1.E, Q2.E, U2.Pin_4, R1.Pin_0, R2.Pin_1, R5.leg1, LED1.common_cathode
  N2: U1.LEFT, Q1.C
  N3: U1.RIGHT, Q2.C
  N4: JACK1.POS, U6.P
  N5: Q1.B, R4.Pin_1, LED1.blue_anode
  N6: Q2.B, R3.Pin_1, LED1.red_anode
  N7: U2.Pin_2, R5.wiper
  N8: U2.Pin_3, R1.Pin_1, U4.O
  N9: U2.Pin_5, R3.Pin_0
  N10: U2.Pin_6, R4.Pin_0
  N11: U2.Pin_7, R2.Pin_0, U5.O
  N12: U2.Pin_8, U4.P, U5.P, R5.leg2, U6.O

// code stored in the sketch: Interval-O-Meter.ino
int focusPin = 1;
int shutterPin = 0;
int delayPin = A3;
int toFocusPin = 4;
int modePin = 2;

bool toFocus;
bool mode;
long delayDuration = 0;

// the setup routine runs once when you press reset:
void setup() {
  // initialize the digital pin as an output.
  pinMode(focusPin, OUTPUT);
  pinMode(shutterPin, OUTPUT);
  pinMode(delayPin, INPUT);
  pinMode(toFocusPin, INPUT);
  pinMode(modePin, INPUT);
  
  
  
}

// the loop routine runs over and over again forever:
void loop() {
  // Read the mode and delay duration only once to prevent accidental changes
  // This also means there can be no intentional changes
  mode = (digitalRead(modePin) == HIGH);
  delayDuration = analogRead(delayPin);
  
  //scale delay for timing between 1 second and 60 seconds
  delayDuration = ((float(delayDuration) / 1023) * (60 - 1) + 1) * 1000;
  
  toFocus = (digitalRead(toFocusPin) == HIGH);
  
  
  if(toFocus) focus();
  if(mode)
    timeLapse();
  else
    starTrail();
}

void focus() {
  digitalWrite(focusPin, HIGH);
  delay(500);
  digitalWrite(focusPin, LOW);
  delay(100);
}

void timeLapse() {
  digitalWrite(shutterPin, HIGH);
  delay(100);
  digitalWrite(shutterPin, LOW);
  delay(delayDuration);
}

void starTrail() {
  digitalWrite(shutterPin, HIGH);
  delay(delayDuration);
  digitalWrite(shutterPin, LOW);
  delay(100);
}
